# Fritzing sketch 2 Potentiometer (saved by Fritzing 0.7.12b)
breadboards: 1

parts:
  Arduino1 = Arduino
  R1 = Resistor [tolerance=±5% resistance=330 package=THT]
  LED1 = LED - 5mm [color="Red (633nm)" package="5 mm [THT]"]
  R3 = Trimmer Potentiometer [maximum_resistance=10kΩ package=THT]

nets:
  N1: Arduino1.D10, LED1.anode
  N2: Arduino1.+5V, R3.leg2
  N3: Arduino1.GND, R1.Pin_0, R3.leg1
  N4: Arduino1.A0, R3.wiper
  N5: R1.Pin_1, LED1.cathode
