# Fritzing sketch 2.5 PhotoResistor (saved by Fritzing 0.7.12b)
breadboards: 1

parts:
  Arduino1 = Arduino
  R1 = Resistor [tolerance=±5% resistance=330 package=THT]
  LED1 = LED - 5mm [color="Red (633nm)" package="5 mm [THT]"]
  R2 = Photocell (LDR) [package=THT]
  R3 = Resistor [tolerance=±5% resistance=10k package=THT]

nets:
  N1: Arduino1.D10, LED1.anode
  N2: Arduino1.+5V, R2.pin_1
  N3: Arduino1.GND, R1.Pin_0, R3.Pin_0
  N4: Arduino1.A0, R2.pin_0, R3.Pin_1
  N5: R1.Pin_1, LED1.cathode
