# Fritzing sketch 3 button (saved by Fritzing 0.7.12b)
breadboards: 1

parts:
  Arduino1 = Arduino
  LED1 = LED - 5mm [color="Red (633nm)" package="5 mm [THT]"]
  R1 = Resistor [tolerance=±5% resistance=330 package=THT]
  S3 = Pushbutton [package=THT]

nets:
  N1: Arduino1.D10, LED1.anode
  N2: Arduino1.D7, S3.leg0
  N3: Arduino1.GND, R1.Pin_0, S3.leg1
  N4: LED1.cathode, R1.Pin_1
