# Fritzing sketch 4.1 PotFadeSerialServo  (saved by Fritzing 0.7.12b)
breadboards: 1

parts:
  Arduino1 = Arduino
  LED1 = LED - 5mm [color="Red (633nm)" package="5 mm [THT]"]
  R1 = Resistor [tolerance=±5% resistance=330 package=THT]
  J2 = Basic Servo
  R3 = Trimmer Potentiometer [maximum_resistance=10kΩ package=THT]

nets:
  N1: Arduino1.D6, LED1.anode
  N2: Arduino1.D5, J2.pulse
  +5V: Arduino1.+5V, J2.vcc, R3.leg2
  GND: Arduino1.GND, R1.Pin_0, J2.gnd, R3.leg1
  N3: Arduino1.A0, R3.wiper
  N4: LED1.cathode, R1.Pin_1
